# Fritzing sketch steampunk-clock (saved by Fritzing 1.0.6)
circuit board: 8.46667cm x 5.64444cm
perfboards: 1

parts:
  Hour_servo = Dagu DGServo 9g (Top view) [part_number=RS001B]
  Minute_servo = Dagu DGServo 9g (Top view) [part_number=RS001B]
  Hour_led = LED - 5mm [color="Yellow (595nm)" current=0.030A package="5 mm [THT]"]
  R1 = Resistor [tolerance=±5% power=0.25W resistance=100 package=THT]
  Minute_led = LED - 5mm [color="Yellow (595nm)" current=0.030A package="5 mm [THT]"]
  R2 = Resistor [tolerance=±5% power=0.25W resistance=100 package=THT]
  Hours = female pin header, 4 pins [form="♀ (female)"]
  Minutes = female pin header, 4 pins [form="♀ (female)"]
  Hour_cable = Header 4 [package=1x04-1mm-ra]
  Minute_cable = Header 4 [package=1x04-1mm-ra]
  U1 = LuaNode32 / ESP32 [part_number=ESP32S-PIN30]
  Settings_button = Momentary Switch [package=ksa_sealed_tac_switch]
  Buzzer = Piezo Buzzer
  Mode_switch = SWITCH-SP3T [package=switch-sp3t-smd]
  ZS-042_RTC2 = ZS-042 RTC Module

nets:
  N1: Hour_servo.gnd, Hour_led.cathode, Hour_cable.2
  N2: Hour_servo.vcc, Hour_cable.3
  N3: Hour_servo.pulse, Hour_cable.4
  N4: Minute_servo.gnd, Minute_led.cathode, Minute_cable.2
  N5: Minute_servo.vcc, Minute_cable.3
  N6: Minute_servo.pulse, Minute_cable.4
  N7: Hour_led.anode, Hour_cable.1
  N8: R1.Pin_0, Hours.pin1
  N9: R1.Pin_1, U1.D12
  N10: Minute_led.anode, Minute_cable.1
  N11: R2.Pin_0, Minutes.pin1
  N12: R2.Pin_1, U1.D13
  GND: Hours.pin2, Minutes.pin2, U1.GND, Settings_button.4, Buzzer.pin_1, ZS-042_RTC2.GND
  N13: Hours.pin3, Minutes.pin3, U1.Vin
  N14: Hours.pin4, U1.RX2
  N15: Minutes.pin4, U1.TX2
  N16: U1.D25, Mode_switch.1
  N17: U1.D26, Mode_switch.2
  N18: U1.D27, Mode_switch.4
  3V3: U1.3V3, Mode_switch.3, ZS-042_RTC2.VCC
  N19: U1.D4, Settings_button.1
  N20: U1.D21, ZS-042_RTC2.SDA
  N21: U1.D22, ZS-042_RTC2.SCL
  N22: U1.D23, Buzzer.pin_2

custom parts:
  LuaNode32 / ESP32: New Image for LuaNode32 DOIT ESP32 DEVKIT V1. Base parts from LuaNode32 / ESP32 ESP32 based LuaNode32 by G.Noorlander DOIT Esp32 DevKit v1 (30 pins long, 11 pins width) by Werner Rothschopf (modified by vanepp Dec 2018)
  Piezo Buzzer: Part from https://www.nutsvolts.com/magazine/article/november2012_SmileysWorkshop. Breadboard and icon images modified to be 0.3" in spacing and be more similar to the actual physical part.
